// Logisim project lab4_ex1.circ as structural Verilog: 6 circuits, main circuit main
module main (
  input  [3:0] A,
  input  [3:0] B,
  input  [2:0] S,
  output Z,
  output Sign_bit,
  output V,
  output Cout
);

  wire _7Seg_sa, _7Seg_sb, _7Seg_sc, _7Seg_sd, _7Seg_se, _7Seg_sf, _7Seg_sg;
  wire [2:0] multiplexer_3_out;
  wire [3:0] Arith__Unit_f, Logic_Unit_f, multiplexer_1_out, multiplexer_2_out, not_1_out, not_2_out;

  assign not_1_out = ~A;  // NOT_Gate not_1, 4 bits wide
  assign not_2_out = ~B;  // NOT_Gate not_2, 4 bits wide
  Multiplexer #(.width(4), .enable("false")) multiplexer_1 (
    .in0(A), .in1(not_1_out), .out(multiplexer_1_out), .sel(S[0]));
  Multiplexer #(.width(4), .enable("false")) multiplexer_2 (
    .in0(B), .in1(not_2_out), .out(multiplexer_2_out), .sel(S[2]));
  AU Arith__Unit (
    .Cin(S[1]), .A(multiplexer_1_out), .B(multiplexer_2_out), .F(Arith__Unit_f), .Overflow(V), .Cout(Cout));
  LED led_1 (.in(Cout));
  LU Logic_Unit (.A(A), .B(multiplexer_2_out), .Y1(S[1]), .Y0(S[0]), .F(Logic_Unit_f));
  LED led_2 (.in(V));
  Multiplexer #(.width(4), .enable("false")) multiplexer_3 (
    .in0(Logic_Unit_f), .in1(Arith__Unit_f), .out({Sign_bit, multiplexer_3_out}), .sel(S[2]));
  nor nor_1 (Z, multiplexer_3_out[0], multiplexer_3_out[1], multiplexer_3_out[2], Sign_bit);
  LED led_3 (.in(Sign_bit));
  _7segpre _7Seg (
    .D0(multiplexer_3_out[0]), .D1(multiplexer_3_out[1]), .D2(multiplexer_3_out[2]), .D3(Sign_bit),
    .Sa(_7Seg_sa), .Sb(_7Seg_sb), .Sc(_7Seg_sc), .Sd(_7Seg_sd), .Se(_7Seg_se), .Sf(_7Seg_sf), .Sg(_7Seg_sg));
  _7_Segment_Display u_7_segment_display_1 (
    .g(_7Seg_sg), .f(_7Seg_sf), .a(_7Seg_sa), .b(_7Seg_sb), .e(_7Seg_se), .d(_7Seg_sd), .c(_7Seg_sc));  // open: dp
endmodule

module adder (
  input  a,
  input  b,
  input  c_in,
  output Sum,
  output c_out
);

  wire AND_2_out, AND_out, XOR_out;

  and AND (AND_out, b, a);
  xor XOR (XOR_out, a, b);
  and AND_2 (AND_2_out, c_in, XOR_out);
  xor XOR_2 (Sum, XOR_out, c_in);
  or OR (c_out, AND_2_out, AND_out);
endmodule

module _7seg (
  input  D0,
  input  D1,
  input  D2,
  input  D3,
  output Sa,
  output Sb,
  output Sc,
  output Sd,
  output Se,
  output Sf,
  output Sg
);

  wire and_1_out, and_2_out, and_3_out, and_4_out, and_5_out, and_6_out, and_7_out, and_8_out, and_9_out,
       and_10_out, and_11_out, and_12_out, and_13_out, and_14_out, and_15_out, and_16_out, not_1_out,
       not_2_out, not_3_out, not_4_out, not_5_out, not_6_out, not_7_out, not_8_out, not_9_out, not_10_out,
       not_11_out, not_12_out, not_13_out, not_14_out, not_15_out, not_16_out, not_17_out, not_18_out,
       not_19_out, not_20_out, not_21_out;

  not not_1 (not_1_out, D1);
  and and_1 (and_1_out, not_1_out, not_2_out);
  not not_2 (not_2_out, D3);
  and and_2 (and_2_out, D1, D3);
  not not_3 (not_3_out, D1);
  not not_4 (not_4_out, D2);
  and and_3 (and_3_out, not_4_out, not_5_out);
  not not_5 (not_5_out, D3);
  and and_4 (and_4_out, D2, D3);
  not not_6 (not_6_out, D2);
  or or_1 (Sc, not_6_out, D3, D1);
  not not_7 (not_7_out, D1);
  and and_5 (and_5_out, not_7_out, not_8_out);
  not not_8 (not_8_out, D3);
  not not_9 (not_9_out, D1);
  and and_6 (and_6_out, not_9_out, D2);
  and and_7 (and_7_out, D2, not_10_out);
  not not_10 (not_10_out, D3);
  not not_11 (not_11_out, D2);
  and and_8 (and_8_out, D1, not_11_out, D3);
  not not_12 (not_12_out, D1);
  and and_9 (and_9_out, not_12_out, not_13_out);
  not not_13 (not_13_out, D3);
  and and_10 (and_10_out, D2, not_14_out);
  not not_14 (not_14_out, D3);
  not not_15 (not_15_out, D2);
  and and_11 (and_11_out, not_15_out, not_16_out);
  not not_16 (not_16_out, D3);
  and and_12 (and_12_out, D1, not_17_out);
  not not_17 (not_17_out, D2);
  and and_13 (and_13_out, D1, not_18_out);
  not not_18 (not_18_out, D3);
  not not_19 (not_19_out, D1);
  and and_14 (and_14_out, not_19_out, D2);
  and and_15 (and_15_out, D1, not_20_out);
  not not_20 (not_20_out, D2);
  and and_16 (and_16_out, D1, not_21_out);
  not not_21 (not_21_out, D3);
  or or_2 (Sa, and_1_out, D2, and_2_out, D0);
  or or_3 (Sb, not_3_out, and_3_out, and_4_out);
  or or_4 (Sd, and_5_out, and_6_out, and_7_out, and_8_out, D0);
  or or_5 (Se, and_9_out, and_10_out);
  or or_6 (Sf, and_11_out, and_12_out, and_13_out, D0);
  or or_7 (Sg, and_14_out, and_15_out, and_16_out, D0);
  _7_Segment_Display u_7_segment_display_1 (.g(Sg), .f(Sf), .a(Sa), .b(Sb), .e(Se), .d(Sd), .c(Sc));  // open: dp
endmodule

module AU (
  input  Cin,
  input  [3:0] A,
  input  [3:0] B,
  output [3:0] F,
  output Overflow,
  output Cout
);

  wire adder_1_cout, adder_2_cout, adder_3_cout;

  Adder #(.width(1)) adder_1 (.a(A[0]), .b(B[0]), .out(F[0]), .cin(Cin), .cout(adder_1_cout));
  Adder #(.width(1)) adder_2 (.a(A[1]), .b(B[1]), .out(F[1]), .cin(adder_1_cout), .cout(adder_2_cout));
  Adder #(.width(1)) adder_3 (.a(A[2]), .b(B[2]), .out(F[2]), .cin(adder_2_cout), .cout(adder_3_cout));
  Adder #(.width(1)) adder_4 (.a(A[3]), .b(B[3]), .out(F[3]), .cin(adder_3_cout), .cout(Cout));
  xor xor_1 (Overflow, adder_3_cout, Cout);
endmodule

module LU (
  input  [3:0] A,
  input  [3:0] B,
  input  Y1,
  input  Y0,
  output [3:0] F
);

  wire [3:0] and_1_out, or_1_out, xnor_1_out, xor_1_out;

  assign and_1_out = A & B;  // AND_Gate and_1, 4 bits wide
  assign or_1_out = A | B;  // OR_Gate or_1, 4 bits wide
  assign xor_1_out = A ^ B;  // XOR_Gate xor_1, 4 bits wide
  assign xnor_1_out = ~(A ^ B);  // XNOR_Gate xnor_1, 4 bits wide
  Multiplexer #(.select(2), .width(4), .enable("false")) multiplexer_1 (
    .in0(and_1_out), .in1(or_1_out), .in2(xor_1_out), .in3(xnor_1_out), .out(F), .sel({Y1, Y0}));
endmodule

module _7segpre (
  input  D0,
  input  D1,
  input  D2,
  input  D3,
  output Sa,
  output Sb,
  output Sc,
  output Sd,
  output Se,
  output Sf,
  output Sg
);

  wire and_1_out, and_2_out, and_3_out, and_4_out, and_5_out, and_6_out, and_7_out, and_8_out, and_9_out,
       and_10_out, and_11_out, and_12_out, and_13_out, and_14_out, and_15_out, and_16_out, not_1_out,
       not_2_out, not_3_out, not_4_out, not_5_out, not_6_out, not_7_out, not_8_out, not_9_out, not_10_out,
       not_11_out, not_12_out, not_13_out, not_14_out, not_15_out, not_16_out, not_17_out, not_18_out,
       not_19_out, not_20_out, not_21_out;

  not not_1 (not_1_out, D1);
  and and_1 (and_1_out, not_1_out, not_2_out);
  not not_2 (not_2_out, D3);
  and and_2 (and_2_out, D1, D3);
  not not_3 (not_3_out, D1);
  not not_4 (not_4_out, D2);
  and and_3 (and_3_out, not_4_out, not_5_out);
  not not_5 (not_5_out, D3);
  and and_4 (and_4_out, D2, D3);
  not not_6 (not_6_out, D2);
  or or_1 (Sc, not_6_out, D3, D1);
  not not_7 (not_7_out, D1);
  and and_5 (and_5_out, not_7_out, not_8_out);
  not not_8 (not_8_out, D3);
  not not_9 (not_9_out, D1);
  and and_6 (and_6_out, not_9_out, D2);
  and and_7 (and_7_out, D2, not_10_out);
  not not_10 (not_10_out, D3);
  not not_11 (not_11_out, D2);
  and and_8 (and_8_out, D1, not_11_out, D3);
  not not_12 (not_12_out, D1);
  and and_9 (and_9_out, not_12_out, not_13_out);
  not not_13 (not_13_out, D3);
  and and_10 (and_10_out, D2, not_14_out);
  not not_14 (not_14_out, D3);
  not not_15 (not_15_out, D2);
  and and_11 (and_11_out, not_15_out, not_16_out);
  not not_16 (not_16_out, D3);
  and and_12 (and_12_out, D1, not_17_out);
  not not_17 (not_17_out, D2);
  and and_13 (and_13_out, D1, not_18_out);
  not not_18 (not_18_out, D3);
  not not_19 (not_19_out, D1);
  and and_14 (and_14_out, not_19_out, D2);
  and and_15 (and_15_out, D1, not_20_out);
  not not_20 (not_20_out, D2);
  and and_16 (and_16_out, D1, not_21_out);
  not not_21 (not_21_out, D3);
  or or_2 (Sa, and_1_out, D2, and_2_out, D0);
  or or_3 (Sb, not_3_out, and_3_out, and_4_out);
  or or_4 (Sd, and_5_out, and_6_out, and_7_out, and_8_out, D0);
  or or_5 (Se, and_9_out, and_10_out);
  or or_6 (Sf, and_11_out, and_12_out, and_13_out, D0);
  or or_7 (Sg, and_14_out, and_15_out, and_16_out, D0);
endmodule
