// Logisim project ex2.circ as structural Verilog: 1 circuit, main circuit main
module main (
  input  a,
  input  b,
  input  c_in,
  output Sum,
  output c_out
);

  wire AND_2_out, AND_out, XOR_out;

  and AND (AND_out, b, a);
  xor XOR (XOR_out, a, b);
  and AND_2 (AND_2_out, c_in, XOR_out);
  xor XOR_2 (Sum, XOR_out, c_in);
  or OR (c_out, AND_2_out, AND_out);
endmodule
