// Logisim project lab_5_ex_1.circ as structural Verilog: 2 circuits, main circuit main
module main (
);

  wire and_1_out, and_2_out, and_3_out, and_4_out, and_5_out, and_6_out, clock_1_out, d_ff_1_q, d_ff_2_q,
       d_ff_3_q, not_1_out, not_2_out, not_3_out, not_4_out, not_5_out, not_6_out, not_7_out, not_8_out,
       not_9_out, or_1_out, or_2_out, or_3_out, seg_1_sa, seg_1_sb, seg_1_sc, seg_1_sd, seg_1_se, seg_1_sf,
       seg_1_sg;

  and and_1 (and_1_out, d_ff_1_q, not_1_out);
  not not_1 (not_1_out, d_ff_2_q);
  not not_2 (not_2_out, d_ff_1_q);
  and and_2 (and_2_out, not_2_out, d_ff_2_q, d_ff_3_q);
  not not_3 (not_3_out, d_ff_2_q);
  and and_3 (and_3_out, not_3_out, d_ff_3_q);
  not not_4 (not_4_out, d_ff_1_q);
  and and_4 (and_4_out, not_4_out, d_ff_2_q, not_5_out);
  not not_5 (not_5_out, d_ff_3_q);
  not not_6 (not_6_out, d_ff_2_q);
  and and_5 (and_5_out, not_6_out, not_7_out);
  not not_7 (not_7_out, d_ff_3_q);
  not not_8 (not_8_out, d_ff_1_q);
  and and_6 (and_6_out, not_8_out, d_ff_2_q, not_9_out);
  not not_9 (not_9_out, d_ff_3_q);
  or or_1 (or_1_out, and_1_out, and_2_out);
  or or_2 (or_2_out, and_3_out, and_4_out);
  or or_3 (or_3_out, and_5_out, and_6_out);
  Clock clock_1 (.out(clock_1_out));
  D_Flip_Flop d_ff_1 (.clk(clock_1_out), .D(or_1_out), .Q(d_ff_1_q));  // open: Qn, preset, en, reset
  D_Flip_Flop d_ff_2 (.clk(clock_1_out), .D(or_2_out), .Q(d_ff_2_q));  // open: Qn, preset, en, reset
  D_Flip_Flop d_ff_3 (.clk(clock_1_out), .D(or_3_out), .Q(d_ff_3_q));  // open: Qn, preset, en, reset
  seg seg_1 (
    .D1(d_ff_1_q), .D2(d_ff_2_q), .D3(d_ff_3_q), .Sa(seg_1_sa), .Sb(seg_1_sb), .Sc(seg_1_sc), .Sd(seg_1_sd),
    .Se(seg_1_se), .Sf(seg_1_sf), .Sg(seg_1_sg));  // open: D0
  _7_Segment_Display u_7_segment_display_1 (
    .g(seg_1_sg), .f(seg_1_sf), .a(seg_1_sa), .b(seg_1_sb), .e(seg_1_se), .d(seg_1_sd), .c(seg_1_sc));  // open: dp
endmodule

module seg (
  input  D0,
  input  D1,
  input  D2,
  input  D3,
  output Sa,
  output Sb,
  output Sc,
  output Sd,
  output Se,
  output Sf,
  output Sg
);

  wire and_1_out, and_2_out, and_3_out, and_4_out, and_5_out, and_6_out, and_7_out, and_8_out, and_9_out,
       and_10_out, and_11_out, and_12_out, and_13_out, and_14_out, and_15_out, and_16_out, not_1_out,
       not_2_out, not_3_out, not_4_out, not_5_out, not_6_out, not_7_out, not_8_out, not_9_out, not_10_out,
       not_11_out, not_12_out, not_13_out, not_14_out, not_15_out, not_16_out, not_17_out, not_18_out,
       not_19_out, not_20_out, not_21_out;

  not not_1 (not_1_out, D1);
  and and_1 (and_1_out, not_1_out, not_2_out);
  not not_2 (not_2_out, D3);
  and and_2 (and_2_out, D1, D3);
  not not_3 (not_3_out, D1);
  not not_4 (not_4_out, D2);
  and and_3 (and_3_out, not_4_out, not_5_out);
  not not_5 (not_5_out, D3);
  and and_4 (and_4_out, D2, D3);
  not not_6 (not_6_out, D2);
  or or_1 (Sc, not_6_out, D3, D1);
  not not_7 (not_7_out, D1);
  and and_5 (and_5_out, not_7_out, not_8_out);
  not not_8 (not_8_out, D3);
  not not_9 (not_9_out, D1);
  and and_6 (and_6_out, not_9_out, D2);
  and and_7 (and_7_out, D2, not_10_out);
  not not_10 (not_10_out, D3);
  not not_11 (not_11_out, D2);
  and and_8 (and_8_out, D1, not_11_out, D3);
  not not_12 (not_12_out, D1);
  and and_9 (and_9_out, not_12_out, not_13_out);
  not not_13 (not_13_out, D3);
  and and_10 (and_10_out, D2, not_14_out);
  not not_14 (not_14_out, D3);
  not not_15 (not_15_out, D2);
  and and_11 (and_11_out, not_15_out, not_16_out);
  not not_16 (not_16_out, D3);
  and and_12 (and_12_out, D1, not_17_out);
  not not_17 (not_17_out, D2);
  and and_13 (and_13_out, D1, not_18_out);
  not not_18 (not_18_out, D3);
  not not_19 (not_19_out, D1);
  and and_14 (and_14_out, not_19_out, D2);
  and and_15 (and_15_out, D1, not_20_out);
  not not_20 (not_20_out, D2);
  and and_16 (and_16_out, D1, not_21_out);
  not not_21 (not_21_out, D3);
  or or_2 (Sa, and_1_out, D2, and_2_out, D0);
  or or_3 (Sb, not_3_out, and_3_out, and_4_out);
  or or_4 (Sd, and_5_out, and_6_out, and_7_out, and_8_out, D0);
  or or_5 (Se, and_9_out, and_10_out);
  or or_6 (Sf, and_11_out, and_12_out, and_13_out, D0);
  or or_7 (Sg, and_14_out, and_15_out, and_16_out, D0);
  _7_Segment_Display u_7_segment_display_1 (.g(Sg), .f(Sf), .a(Sa), .b(Sb), .e(Se), .d(Sd), .c(Sc));  // open: dp
endmodule
