// Logisim project ex1.circ as structural Verilog: 1 circuit, main circuit main
module main (
  input  z,
  input  x,
  input  y,
  input  w,
  input  z_2,
  input  x_2,
  input  y_2,
  input  w_2,
  output out_9
);

  wire not_1_out, not_2_out, not_3_out, not_4_out, or_1_out, or_2_out, w_prime_xy_out, wx_prime_y_out,
       wxy_out, x_prime_y_prime_z_out, xy_prime_z_out, y_prime_z_out, yw_out, yx_out;

  not not_1 (not_1_out, y_2);
  not not_2 (not_2_out, x);
  not not_3 (not_3_out, y);
  not not_4 (not_4_out, w);
  and y_prime_z (y_prime_z_out, not_1_out, z_2);
  and yx (yx_out, y_2, x_2);
  and yw (yw_out, y_2, w_2);
  and xy_prime_z (xy_prime_z_out, x, not_3_out, z);
  and x_prime_y_prime_z (x_prime_y_prime_z_out, not_2_out, not_3_out, z);
  and w_prime_xy (w_prime_xy_out, x, not_4_out, y);
  and wx_prime_y (wx_prime_y_out, w, not_2_out, y);
  and wxy (wxy_out, w, x, y);
  or or_1 (or_1_out, xy_prime_z_out, x_prime_y_prime_z_out, w_prime_xy_out, wx_prime_y_out, wxy_out);
  or or_2 (or_2_out, y_prime_z_out, yx_out, yw_out);
  xnor xnor_1 (out_9, or_1_out, or_2_out);
endmodule
