// Logisim project ex2.circ as structural Verilog: 1 circuit, main circuit main
module main (
  input  [1:0] A,
  input  [1:0] B,
  output [3:0] M
);

  wire A0B1_out, A1B0_out, A1B1_out, and_1_out;

  and A0B0 (M[0], A[0], B[0]);
  and A0B1 (A0B1_out, A[0], B[1]);
  and A1B0 (A1B0_out, A[1], B[0]);
  and A1B1 (A1B1_out, A[1], B[1]);
  xor xor_1 (M[1], A0B1_out, A1B0_out);
  and and_1 (and_1_out, A0B1_out, A1B0_out);
  xor xor_2 (M[2], and_1_out, A1B1_out);
  and and_2 (M[3], and_1_out, A1B1_out);
endmodule
