// Logisim project ex3.circ as structural Verilog: 1 circuit, main circuit main
module main (
  input  [2:0] A,
  input  [1:0] B,
  output [4:0] M
);

  wire A0B1_out, A1B0_out, A1B1_out, A2B0_out, A2B1_out, and_1_out, and_2_out, and_4_out, or_1_out, xor_2_out;

  and A0B0 (M[0], A[0], B[0]);
  and A0B1 (A0B1_out, A[0], B[1]);
  and A1B0 (A1B0_out, B[0], A[1]);
  and A1B1 (A1B1_out, A[1], B[1]);
  and A2B0 (A2B0_out, A[2], B[0]);
  and A2B1 (A2B1_out, A[2], B[1]);
  xor xor_1 (M[1], A0B1_out, A1B0_out);
  and and_1 (and_1_out, A0B1_out, A1B0_out);
  xor xor_2 (xor_2_out, A1B1_out, A2B0_out);
  and and_2 (and_2_out, A1B1_out, A2B0_out);
  xor xor_3 (M[3], A2B1_out, or_1_out);
  and and_3 (M[4], A2B1_out, or_1_out);
  xor xor_4 (M[2], xor_2_out, and_1_out);
  and and_4 (and_4_out, and_1_out, xor_2_out);
  or or_1 (or_1_out, and_4_out, and_2_out);
endmodule
